# Fritzing sketch Portal Gun Part 1 (saved by Fritzing 0.9.3b)

parts:
  Part1 = adafruit [part_number=1426]
  R1 = Resistor [tolerance=±5% resistance=470 package="0603 [SMD]"]
  Part2 = Arduino Uno (Rev3) - ICSP
  S1 = Pushbutton [package="[SMD]"]
  S2 = Pushbutton [package="[SMD]"]

nets:
  N1: Part1.connector24, Part2.5V
  N2: Part1.connector25, R1.Pin_1
  N3: Part1.connector26, Part2.GND, S1.Pin_3, S1.Pin_4, S2.Pin_3, S2.Pin_4
  N4: R1.Pin_0, Part2.D6_PWM
  N5: Part2.D2, S2.Pin_1, S2.Pin_2
  N6: Part2.D3_PWM, S1.Pin_1, S1.Pin_2
